// Logisim project main.circ as structural Verilog: 2 circuits, main circuit main
module main (
  input  [11:0] PC,
  output [3:0] out_2,
  output [3:0] out_3,
  output [3:0] out_4,
  output [3:0] out_5,
  output [63:0] out_6,
  output [11:0] out_7
);

  wire clock_1_out;
  wire [11:0] register_1_q;

  Clock clock_1 (.out(clock_1_out));
  Register #(.width(12)) register_1 (.D(out_7), .en(clock_1_out), .clk(clock_1_out), .Q(register_1_q));  // open: clr
  Fetch fetch_1 (.PC(register_1_q), .icode(out_2), .ifun(out_3), .rA(out_4), .rB(out_5), .valC(out_6), .valP(out_7));
endmodule

module Fetch (
  input  [11:0] PC,
  output [3:0] icode,
  output [3:0] ifun,
  output [3:0] rA,
  output [3:0] rB,
  output [63:0] valC,
  output [11:0] valP
);

  wire adder_1_cout, adder_2_cout;
  wire [1:0] rom_2_data;
  wire [3:0] and_1_out, multiplexer_3_out;
  wire [3:3] or_1_out;
  wire [7:0] code_p3, undriven, undriven_2, undriven_3, undriven_4, undriven_5, undriven_6, undriven_7,
       undriven_8;
  wire [11:0] rom_1_p1;

  // NoConnect on adder_1_cout
  // ROM #(.addrWidth(12), .line("dual"), .misaligned("true")) code: pin names not known; wires that end beside it: 12'h1e, PC, code_p3
  // ROM #(.addrWidth(12), .line("octo"), .misaligned("true")) rom_1: pin names not known; wires that end beside it: rom_1_p1
  Adder #(.width(12)) adder_1 (.a(PC), .b(12'h2), .out(rom_1_p1), .cin(1'b0), .cout(adder_1_cout));
  ROM #(.addrWidth(4), .dataWidth(2)) rom_2 (.addr(icode), .data(rom_2_data));
  Multiplexer #(.select(2), .width(8)) multiplexer_1 (
    .in0({8{1'b0}}), .in1(code_p3), .in2({8{1'b0}}), .in3(code_p3), .out({rB, rA}), .sel(rom_2_data));
  Multiplexer #(.select(2), .width(64)) multiplexer_2 (
    .in0({64{1'b0}}), .in1({64{1'b0}}),
    .in2({undriven_8, undriven_7, undriven_6, undriven_5, undriven_4, undriven_3, undriven_2, code_p3}),
    .in3({undriven, undriven_8, undriven_7, undriven_6, undriven_5, undriven_4, undriven_3, undriven_2}),
    .out(valC), .sel(rom_2_data));
  Multiplexer #(.select(2), .width(4)) multiplexer_3 (
    .in0(4'b0001), .in1(4'b0010), .in2(4'b1001), .in3(4'b1010), .out(multiplexer_3_out), .sel(rom_2_data));
  or or_1 (or_1_out[3], icode[0], icode[1], icode[2], icode[3]);
  assign and_1_out = {4{or_1_out[3]}} & multiplexer_3_out;  // AND_Gate and_1, 4 bits wide
  // NoConnect on adder_2_cout
  Adder #(.width(12)) adder_2 (.a({{8{1'b0}}, and_1_out}), .b(PC), .out(valP), .cout(adder_2_cout));  // open: cin

  // Notes on the sheet:
  //   contents of code (hex, n*v repeats v):
  //   30 f2 19 fc 6*ff 30 f1 e7 3 6*0 30 f6 8*0 30 f8 1 7*0 30 f9 5 7*0 20 6a 61 9a 75 54 7*0 20 6b 60 bb
  //   20 b2 60 8b 20 b1 60 86 70 32
  //   contents of rom_1 (hex, n*v repeats v):
  //   30 f2 19 fc 6*ff 30 f1 e7 3 6*0 30 f6 8*0 30 f8 1 7*0 30 f9 5 7*0 20 6a 61 9a 75 54 7*0 20 6b 60 bb
  //   20 b2 60 8b 20 b1 60 86 70 32
  //   8-15 vals?
  //   0-7, icode ifun
  //   contents of rom_2 (hex, n*v repeats v):
  //   0 0 1 3 3 3 1 2 2 0 1 1
  //   PC + 00: +1, 01: +2, 10: +9, 11: +10
endmodule
